# Fritzing sketch rajasthan hackathon (saved by Fritzing 0.9.3b)
breadboards: 1

parts:
  U1 = ADXL335 [package=lfcsp-16]
  Part1 = Arduino Uno (Rev3)
  LCD1 = LCD screen
  Part2 = Flora GPS
  U2 = POT [package=pot_alpha_rv16af-20]
  Part3 = Adafruit FONA - Mini Cellular GSM Breakout
  VCC1 = 4 x AAA Battery Mount
  VCC2 = Battery

nets:
  GND: U1.COM, Part1.GND, LCD1.VSS, Part2.GND, U2.S, U2.E, Part3.GND, VCC1.-, VCC2.-
  N1: U1.ZOUT, Part1.A3
  N2: U1.YOUT, Part1.A2
  N3: U1.XOUT, Part1.A1
  N4: U1.VS, LCD1.VDD, LCD1.LED+
  N5: Part1.D8, LCD1.DB6
  N6: Part1.D9_PWM, LCD1.DB7
  N7: Part1.D10_PWM/SS, Part2.TX
  N8: Part1.D2, Part3.TXD_5V
  N9: Part1.D3_PWM, Part3.RXD_5V
  N10: Part1.D4, LCD1.RS
  N11: Part1.D5_PWM, LCD1.E
  N12: Part1.D6_PWM, LCD1.DB4
  N13: Part1.D7, LCD1.DB5
  N14: Part1.5V, Part3.VCCIO
  N15: Part2.3.3V, VCC2.+

custom parts:
  Flora GPS: This module is the best way to add a GPS to your wearable project. It's part of the Adafruit Flora series of wearable electronics, designed specifically for use with the Flora motherboard. Installed on the PCB is the latest of our Ultimate GPS modules, a small, super-thin, low power GPS module with built in data-logging capability!
  Adafruit FONA - Mini Cellular GSM Breakout: An all-in-one cellular phone module that lets you add voice, text, SMS and GPRS data to your project. Quad-band 850/900/1800/1900MHz - connect onto any global GSM network with any 2G SIM. Includes an onboard LiPoly battery charging circuitry so you can take your project on the go. Also works as an FM radio receiver.

// code stored in the sketch: rajasthan hackathon.fzz.ino
LiquidCrystal lcd(7, 6, 5, 4 3, 2);

#include <SoftwareSerial.h>
SoftwareSerial gps(10,11); // RX, TX
char str[70];
String gpsString="";

//Code of (Liquid Crystral display)LCD
//First we define pins for LCD & software serial communication.
//Software Serial Library is used to allow serial communication on pin 10 and 11.

#include<LiquidCrystal.h>
LiquidCrystal lcd(7, 6, 5, 4, 3, 2);
#include <SoftwareSerial.h>
SoftwareSerial gps(10,11); // RX, TX
char str[70];
String gpsString="";

//LCD, GSM & GPS module in setup function and showed a welcome message on LCD.
void setup() 
{
  lcd.begin(16,2);
  Serial.begin(9600);
  gps.begin(9600);
  lcd.print("Vehicle Tracking");
  lcd.setCursor(0,1);


//In loop we receive message and GPS string.

void loop()
{
  serialEvent();
  if(temp)
  {
    get_gps();
    tracking();
  }
}

//Functions void init_sms and void send_sms() are used to initialising and sending message. Use proper 10 digit Cell phone no, in init_sms function.  

//Function void get_gps() has been used to extract the coordinates from the received string.

//Function void gpsEvent() is used for receiving GPS data into the Arduino.

//Function void serialEvent() is used for receiving message from GSM and comparing the received message with predefined message (Track Vehicle).

void serialEvent()
{
  while(Serial.available())
  {
    if(Serial.find("Track Vehicle"))
    {
      temp=1;
      break;
    }

//Initialization function ?gsm_init()? is used for initialising and configuring the GSM Module, where firstly, GSM module is checked whether it is connected or not by sending ?AT? command to GSM module. If response OK is received, means it is ready. System keeps checking for the module until it becomes ready or until ?OK? is received. Then ECHO is turned off by sending the ATE0 command, otherwise GSM module will echo all the commands. Then finally Network availability is checked through the ?AT+CPIN?? command, if inserted card is SIM card and PIN is present, it gives the response +CPIN: READY. This is also check repeatedly until the network is found. This can be clearly understood by the Video belo

//Check all the above functions in Code Section below.
 
#include<LiquidCrystal.h>
LiquidCrystal lcd(7, 6, 5, 4, 3, 2);

#include <SoftwareSerial.h>
SoftwareSerial gps(10,11); // RX, TX

//String str="";
char str[70];
String gpsString="";

char *test="$GPGGA";

String latitude="No Range      ";
String longitude="No Range     ";

int temp=0,i;
boolean gps_status=0;

void setup() 
{
  lcd.begin(16,2);
  Serial.begin(9600);
  gps.begin(9600);

  lcd.print("Vehicle Tracking");
  lcd.setCursor(0,1);
  lcd.print("    System      ");
  delay(2000);
  gsm_init();
  lcd.clear();
  Serial.println("AT+CNMI=2,2,0,0,0");
  lcd.print("GPS Initializing");
  lcd.setCursor(0,1);
  lcd.print("  No GPS Range  ");
  get_gps();
  delay(2000);
  lcd.clear();
  lcd.print("GPS Range Found");
  lcd.setCursor(0,1);
  lcd.print("GPS is Ready");
  delay(2000);
  lcd.clear();
  lcd.print("System Ready");
  temp=0;
}

void loop()
{
  serialEvent();
  if(temp)
  {
    get_gps();
    tracking();
  }
}

void serialEvent()
{
  while(Serial.available())
  {
    if(Serial.find("Track Vehicle"))
    {
      temp=1;
      break;
    }
    else
    temp=0;
  }
}

void gpsEvent()
{
  gpsString="";
  while(1)
  {
   while (gps.available()>0)            //checking serial data from GPS
   {
    char inChar = (char)gps.read();
     gpsString+= inChar;                    //store data from GPS into gpsString
     i++;
     if (i < 7)                      
     {
      if(gpsString[i-1] != test[i-1])         //checking for $GPGGA sentence
      {
        i=0;
        gpsString="";
      }
     }
    if(inChar=='\r')
    {
     if(i>65)
     {
       gps_status=1;
       break;
     }
     else
     {
       i=0;
     }
    }
  }
   if(gps_status)
    break;
  }
}

void gsm_init()
{
  lcd.clear();
  lcd.print("Finding Module..");
  boolean at_flag=1;
  while(at_flag)
  {
    Serial.println("AT");
    while(Serial.available()>0)
    {
      if(Serial.find("OK"))
      at_flag=0;
    }
    
    delay(1000);
  }

  lcd.clear();
  lcd.print("Module Connected..");
  delay(1000);
  lcd.clear();
  lcd.print("Disabling ECHO");
  boolean echo_flag=1;
  while(echo_flag)
  {
    Serial.println("ATE0");
    while(Serial.available()>0)
    {
      if(Serial.find("OK"))
      echo_flag=0;
    }
    delay(1000);
  }

  lcd.clear();
  lcd.print("Echo OFF");
  delay(1000);
  lcd.clear();
  lcd.print("Finding Network..");
  boolean net_flag=1;
  while(net_flag)
  {
    Serial.println("AT+CPIN?");
    while(Serial.available()>0)
    {
      if(Serial.find("+CPIN: READY"))
      net_flag=0;
    }
    delay(1000);
  }
  lcd.clear();
  lcd.print("Network Found..");
  delay(1000);
  lcd.clear();
}

void get_gps()
{
   gps_status=0;
   int x=0;
   while(gps_status==0)
   {
    gpsEvent();
    int str_lenth=i;
    latitude="";
    longitude="";
    int comma=0;
    while(x<str_lenth)
    {
      if(gpsString[x]==',')
      comma++;
      if(comma==2)        //extract latitude from string
      latitude+=gpsString[x+1];     
      else if(comma==4)        //extract longitude from string
      longitude+=gpsString[x+1];
      x++;
    }
    int l1=latitude.length();
    latitude[l1-1]=' ';
    l1=longitude.length();
    longitude[l1-1]=' ';
    lcd.clear();
    lcd.print("Lat:");
    lcd.print(latitude);
    lcd.setCursor(0,1);
    lcd.print("Long:");
    lcd.print(longitude);
    i=0;x=0;
    str_lenth=0;
    delay(2000);
   }
}

void init_sms()
{
  Serial.println("AT+CMGF=1");
  delay(400);
  Serial.println("AT+CMGS=\"+91**********\"");   // use your 10 digit cell no. here
  delay(400);
}

void send_data(String message)
{
  Serial.println(message);
  delay(200);
}

void send_sms()
{
  Serial.write(26);
}

void lcd_status()
{
  lcd.clear();
  lcd.print("Message Sent");
  delay(2000);
  lcd.clear();
  lcd.print("System Ready");
  return;
}

void tracking()
{
    init_sms();
    send_data("Vehicle Tracking Alert:");
    send_data("Your Vehicle Current Location is:");
    Serial.print("Latitude:");
    send_data(latitude);
    Serial.print("Longitude:");
    send_data(longitude);
    send_data("Please take some action soon..\nThankyou");
    send_sms();
    delay(2000);
    lcd_status();
}
